# Fritzing sketch AR01_AR08 (saved by Fritzing 0.9.3b)
breadboards: 1

parts:
  Matrix_keypad1 = KEYPAD 4x4
  Part1 = Arduino Uno (Rev3)
  J1 = Basic Servo
  LED1 = smd LED [color="Red (633nm)" package="1206 [SMD]"]
  LED2 = smd LED [color="Green (555nm)" package="1206 [SMD]"]
  R1 = Resistor [tolerance=±5% resistance=330 package=THT]
  R2 = Resistor [tolerance=±5% resistance=330 package=THT]
  J2 = Piezo Speaker

nets:
  N1: Matrix_keypad1.col1, Part1.D2
  N2: Matrix_keypad1.col2, Part1.D3_PWM
  N3: Matrix_keypad1.col3, Part1.D4
  N4: Matrix_keypad1.col4, Part1.D5_PWM
  N5: Matrix_keypad1.row1, Part1.D6_PWM
  N6: Matrix_keypad1.row2, Part1.D7
  N7: Matrix_keypad1.row3, Part1.D8
  N8: Matrix_keypad1.row4, Part1.D9_PWM
  N9: Part1.D10_PWM/SS, J1.pulse
  N10: Part1.D11_PWM/MOSI, J2.pin2
  N11: Part1.D12/MISO, R2.Pin_0
  N12: Part1.D13/SCK, R1.Pin_0
  5V: Part1.5V, J1.vcc
  GND: Part1.GND, J1.gnd, LED1.cathode, LED2.cathode, J2.pin1
  N13: LED1.anode, R1.Pin_1
  N14: LED2.anode, R2.Pin_1

custom parts:
  KEYPAD 4x4: Matrix keypad 16 buttons, 4 rows x 4 columns
