# Fritzing sketch AR02,AR03 (saved by Fritzing 0.9.3b)
breadboards: 1

parts:
  부품1 = Arduino Uno (Rev3)
  LED1 = LED - 5mm [color="Green (565nm)" package="5 mm [THT]"]
  R1 = Resistor [tolerance=±5% resistance=330 package=THT]
  hc-sr1 = hc-sr04
  hc-sr2 = hc-sr04
  부품2 = LCD1602-I2C
  Generic_4x4_button_keypad1 = Generic 4x4 Keypad
  J1 = Basic Servo

nets:
  N1: 부품1.A0, R1.Pin_1
  N2: 부품1.A4/SDA, 부품2.SDA
  N3: 부품1.A5/SCL, 부품2.SCL
  N4: 부품1.D8, Generic_4x4_button_keypad1.R3
  N5: 부품1.D9_PWM, J1.pulse
  N6: 부품1.D10_PWM/SS, hc-sr1.Echo
  N7: 부품1.D11_PWM/MOSI, hc-sr1.Trig
  N8: 부품1.D12/MISO, hc-sr2.Echo
  N9: 부품1.D13/SCK, hc-sr2.Trig
  N10: 부품1.D2, Generic_4x4_button_keypad1.C4
  N11: 부품1.D3_PWM, Generic_4x4_button_keypad1.C3
  N12: 부품1.D4, Generic_4x4_button_keypad1.C2
  N13: 부품1.D5_PWM, Generic_4x4_button_keypad1.C1
  N14: 부품1.D6_PWM, Generic_4x4_button_keypad1.R1
  N15: 부품1.D7, Generic_4x4_button_keypad1.R2
  VCC: 부품1.5V, hc-sr1.VCC, hc-sr2.VCC, 부품2.VCC, J1.vcc
  GND: 부품1.GND, LED1.cathode, LED1.anode, R1.Pin_0, hc-sr1.GND, hc-sr2.GND, 부품2.GND

custom parts:
  LCD1602-I2C: A standard character display, usually with 2x16 characters. Comes in many colors with LCM1602 IIC attached.
  Generic 4x4 Keypad: generic 4x4 keypad 4 rows of four 6 mm tact switches cheap and nasty but works
