# Fritzing sketch HeartRate (saved by Fritzing 0.9.3b)
breadboards: 1

parts:
  부품1 = LCD1602-I2C
  부품2 = Arduino Uno (Rev3)
  J1 = Piezo Speaker
  S2 = Pushbutton [package="[SMD]"]
  부품4 = Thumb Joystick
  8x8_LED_Modul_mit_MAX1 = 8x8 LED Modul mit MAX7219 [package=THT]
  SEN1 = Pulse Sensor [package=SIP-3]

nets:
  GND: 부품1.GND, 부품2.GND, J1.pin1, S2.Pin_1, S2.Pin_2, 부품4.GND, 8x8_LED_Modul_mit_MAX1.GND_Eingang, SEN1.GND
  VCC: 부품1.VCC, 부품2.5V, 부품4.SEL, 8x8_LED_Modul_mit_MAX1.VCC_Eingang, SEN1.VCC
  N1: 부품1.SDA, 부품2.A4/SDA
  N2: 부품1.SCL, 부품2.A5/SCL
  N3: 부품2.A0, SEN1.Signal
  N4: 부품2.A1, 부품4.HORZ
  N5: 부품2.A2, 부품4.VERT
  N6: 부품2.D11_PWM/MOSI, J1.pin2
  N7: 부품2.D12/MISO, S2.Pin_3, S2.Pin_4
  N8: 부품2.D2, 8x8_LED_Modul_mit_MAX1.CS_Eingang
  N9: 부품2.D3_PWM, 8x8_LED_Modul_mit_MAX1.CLK_Eingang
  N10: 부품2.D4, 8x8_LED_Modul_mit_MAX1.DIN_Eingang
  N11: 부품2.D5_PWM, 부품4.VCC

custom parts:
  LCD1602-I2C: A standard character display, usually with 2x16 characters. Comes in many colors with LCM1602 IIC attached.
  Pulse Sensor: Pulse Sensor Optical Heart Beat Sensor
