# Fritzing sketch RC_Car (saved by Fritzing 0.9.3b)
breadboards: 1

parts:
  부품1 = Arduino Uno (Rev3)
  S1 = H-Bridge with L298N
  부품2 = SRF05 Ultrasonic Rangefinder
  R1 = Photocell (LDR) [package=THT]
  R2 = Resistor [tolerance=±5% resistance=220 package=THT]
  S2 = Pushbutton [package="[THT]"]
  S3 = Pushbutton [package="[THT]"]
  R3 = Resistor [tolerance=±5% resistance=220 package=THT]
  LED1 = LED - 5mm [color="White (6500K)" package="5 mm [THT]"]
  DHT1 = DHT11 Humitidy and Temperature Sensor
  M1 = DC Motor
  M2 = DC Motor
  M3 = DC Motor
  M4 = DC Motor

nets:
  N1: 부품1.A0, R1.pin_0, R2.Pin_1
  N2: 부품1.D8, S1.IN1
  N3: 부품1.D9_PWM, S1.ENA
  N4: 부품1.D10_PWM/SS, S2.Pin_1, S2.Pin_2
  N5: 부품1.D11_PWM/MOSI, S3.Pin_1, S3.Pin_2
  N6: 부품1.D12/MISO, 부품2.Trig
  N7: 부품1.D13/SCK, 부품2.Echo
  N8: 부품1.D2, DHT1.DATA
  N9: 부품1.D3_PWM, LED1.anode
  N10: 부품1.D4, S1.IN3
  N11: 부품1.D5_PWM, S1.IN4
  N12: 부품1.D6_PWM, S1.ENB
  N13: 부품1.D7, S1.IN2
  GND: S1.GND, 부품2.GND, R1.pin_1, S2.Pin_3, S2.Pin_4, S3.Pin_3, S3.Pin_4, R3.Pin_0, DHT1.GND
  N14: S1.M1-01, M1.pin_1, M2.pin_1
  N15: S1.M1-02, M1.pin_2, M2.pin_2
  N16: S1.M2-01, M3.pin_2, M4.pin_2
  N17: S1.M2-02, M3.pin_1, M4.pin_1
  VCC: 부품2.VCC, R2.Pin_0, DHT1.VDD
  N18: R3.Pin_1, LED1.cathode

custom parts:
  H-Bridge with L298N: h-bridge
  DHT11 Humitidy and Temperature Sensor: DHT11 Humidity and Temperature Sensor
