# Fritzing sketch Agility_game_circuit (saved by Fritzing 0.9.3b)
breadboards: 1

parts:
  부품1 = Arduino Uno (Rev3)
  LED1 = LED - 5mm [color="Red (633nm)" package="5 mm [THT]"]
  LED2 = LED - 5mm [color="Orange (612nm)" package="5 mm [THT]"]
  LED3 = LED - 5mm [color="Yellow (595nm)" package="5 mm [THT]"]
  LED4 = LED - 5mm [color="Green (560nm)" package="5 mm [THT]"]
  LED5 = LED - 5mm [color="Blue (470nm)" package="5 mm [THT]"]
  R1 = Resistor [tolerance=±5% resistance=330 package=THT]
  S1 = Pushbutton [package="[THT]"]
  LCD1 = LCD screen
  R2 = Resistor [tolerance=±5% resistance=330 package=THT]
  R3 = Resistor [tolerance=±5% resistance=330 package=THT]
  R4 = Resistor [tolerance=±5% resistance=330 package=THT]
  R5 = Resistor [tolerance=±5% resistance=330 package=THT]

nets:
  N1: 부품1.A4/SDA, LCD1.V0
  N2: 부품1.A5/SCL, LCD1.RS
  N3: 부품1.D8, S1.Pin_3, S1.Pin_4
  GND: 부품1.GND, R1.Pin_0, LCD1.VSS, R2.Pin_0, R3.Pin_0, R4.Pin_0, R5.Pin_0
  N4: 부품1.D2, LED1.anode
  N5: 부품1.D3_PWM, LED2.anode
  N6: 부품1.D4, LED3.anode
  N7: 부품1.D5_PWM, LED4.anode
  N8: 부품1.D6_PWM, LED5.anode
  5V: 부품1.5V, S1.Pin_1, S1.Pin_2, LCD1.VDD
  N9: LED1.cathode, R1.Pin_1
  N10: LED2.cathode, R2.Pin_1
  N11: LED3.cathode, R3.Pin_1
  N12: LED4.cathode, R4.Pin_1
  N13: LED5.cathode, R5.Pin_1
