# Fritzing sketch RandomDice (saved by Fritzing 0.9.3b)
breadboards: 1

parts:
  LCD2 = LCD screen
  LCM1602_IIC2 = LCM1602 IIC [part_number="LCM1602 IIC" chip_label="LCM1602 IIC" package="DIP (Dual Inline) [THT]"]
  부품1 = Arduino Uno (Rev3)
  S1 = Pushbutton [package="[THT]"]
  R3 = Resistor [tolerance=±5% resistance=220 package=THT]
  R6 = Resistor [tolerance=±5% resistance=220 package=THT]
  R7 = Resistor [tolerance=±5% resistance=220 package=THT]
  LED1 = LED - 5mm [color="Blue (505nm)" package="5 mm [THT]"]
  LED8 = LED - 5mm [color="Blue (505nm)" package="5 mm [THT]"]
  LED9 = LED - 5mm [color="Blue (505nm)" package="5 mm [THT]"]
  LED10 = LED - 5mm [color="Blue (505nm)" package="5 mm [THT]"]
  LED11 = LED - 5mm [color="Blue (505nm)" package="5 mm [THT]"]
  LED12 = LED - 5mm [color="Blue (505nm)" package="5 mm [THT]"]
  LED13 = LED - 5mm [color="Blue (505nm)" package="5 mm [THT]"]
  R8 = Resistor [tolerance=±5% resistance=220 package=THT]
  R9 = Resistor [tolerance=±5% resistance=220 package=THT]
  R10 = Resistor [tolerance=±5% resistance=220 package=THT]
  R11 = Resistor [tolerance=±5% resistance=220 package=THT]
  S2 = Pushbutton [package="[THT]"]

nets:
  VSS: LCD2.VSS, LCM1602_IIC2.VSS
  VDD: LCD2.VDD, LCM1602_IIC2.VDD
  N1: LCD2.V0, LCM1602_IIC2.V0
  N2: LCD2.RS, LCM1602_IIC2.RS
  N3: LCD2.R/W, LCM1602_IIC2.RW
  N4: LCD2.E, LCM1602_IIC2.E
  N5: LCD2.DB0, LCM1602_IIC2.D0
  N6: LCD2.DB1, LCM1602_IIC2.D1
  N7: LCD2.DB2, LCM1602_IIC2.D2
  N8: LCD2.DB3, LCM1602_IIC2.D3
  N9: LCD2.DB4, LCM1602_IIC2.D4
  N10: LCD2.DB5, LCM1602_IIC2.D5
  N11: LCD2.DB6, LCM1602_IIC2.D6
  N12: LCD2.DB7, LCM1602_IIC2.D7
  N13: LCD2.LED+, LCM1602_IIC2.A
  N14: LCD2.LED-, LCM1602_IIC2.K
  GND: LCM1602_IIC2.GND, 부품1.GND, S1.Pin_1, S1.Pin_2, R6.Pin_1, R7.Pin_1, R8.Pin_1, R9.Pin_1, S2.Pin_3, S2.Pin_4
  VCC: LCM1602_IIC2.VCC, 부품1.5V
  N15: LCM1602_IIC2.SDA, 부품1.A4/SDA
  N16: LCM1602_IIC2.SCL, 부품1.A5/SCL
  N17: LCM1602_IIC2.LED_A, LCM1602_IIC2.LED_B
  N18: 부품1.D8, LED8.anode
  N19: 부품1.D9_PWM, S2.Pin_1, S2.Pin_2
  N20: 부품1.D10_PWM/SS, S1.Pin_3, S1.Pin_4
  N21: 부품1.D2, LED11.anode
  N22: 부품1.D3_PWM, LED12.anode
  N23: 부품1.D4, LED13.anode
  N24: 부품1.D5_PWM, LED9.anode
  N25: 부품1.D6_PWM, LED10.anode
  N26: 부품1.D7, LED1.cathode
  N27: R3.Pin_0, R10.Pin_0, R11.Pin_0
  N28: R3.Pin_1, LED8.cathode
  N29: R6.Pin_0, LED11.cathode
  N30: R7.Pin_0, LED1.anode
  N31: LED9.cathode, R11.Pin_1
  N32: LED10.cathode, R10.Pin_1
  N33: LED12.cathode, R8.Pin_0
  N34: LED13.cathode, R9.Pin_0

custom parts:
  LCM1602 IIC: I2C-Module to use a 1602 or 2004 LCD on with the wire.h libory Serial LCD Modul
