# Fritzing sketch 본체회로 (saved by Fritzing 0.9.3b)
breadboards: 1

parts:
  부품1 = Arduino Uno (Rev3) - ICSP
  U1 = L9110 H-bridge module [part_number="L9110 H-bridge"]
  M1 = DC Motor
  M2 = DC Motor
  VCC3 = Battery  # not connected
  VCC4 = Battery  # not connected
  VCC5 = Battery  # not connected
  부품2 = Bluetooth HM-10

nets:
  N1: 부품1.D9_PWM, U1.A-IA
  N2: 부품1.D10_PWM/SS, U1.A-IB
  N3: 부품1.D2, 부품2.TXD
  N4: 부품1.D3_PWM, 부품2.RXD
  N5: 부품1.D5_PWM, U1.B-IA
  N6: 부품1.D6_PWM, U1.B-IB
  VCC: 부품1.5V, U1.VCC, 부품2.VCC
  GND: 부품1.GND, U1.GND, 부품2.GND
  N7: U1.MOTOR_A-A, M2.pin_2
  N8: U1.MOTOR_A-B, M2.pin_1
  N9: U1.MOTOR_B-A, M1.pin_2
  N10: U1.MOTOR_B-B, M1.pin_1
