# Fritzing sketch 조종기회로 (saved by Fritzing 0.9.3b)
breadboards: 1

parts:
  부품2 = Bluetooth HM-10
  부품3 = Black Joystick KY-023
  VCC1 = Battery block 9V  # not connected
  부품4 = Arduino Uno (Rev3) - ICSP

nets:
  N1: 부품2.RXD, 부품4.D3_PWM
  N2: 부품2.TXD, 부품4.D2
  GND: 부품2.GND, 부품3.GND, 부품4.GND
  VCC: 부품2.VCC, 부품3.+5V, 부품4.5V
  N3: 부품3.VRy, 부품4.A1
  N4: 부품3.VRx, 부품4.A0

custom parts:
  Black Joystick KY-023: Description: The joystick is a combination of 2 analoog potentiometer and a digital switch. Arduino GND --> Module pin - Arduino +5V --> Module pin +5V Arduino Analoog 0 --> Module VRx Arduino Analoog 1 --> Module VRy Arduino Digital --> Module SW Dimensions: 1" x 1.25"
